# Fritzing sketch factory_sketch (saved by Fritzing 0.9.5d)
breadboards: 1

parts:
  A1 = Raspberry Pi 5
  IC1 = ULN2003A [package="DIP16 [THT]"]
  R1 = Resistor [tolerance=±5% resistance=220 package="1206 [SMD]"]
  S4 = Pushbutton [package="[THT]"]
  R2 = PHOTOCELL [package=photocell-kit]
  R4 = Resistor [tolerance=±5% resistance=10k package=THT]
  R5 = Resistor [tolerance=±5% resistance=10k package=THT]
  R6 = Resistor [tolerance=±5% resistance=10k package=THT]
  R7 = Resistor [tolerance=±5% resistance=10k package=THT]
  R8 = PHOTOCELL [package=photocell-kit]
  R9 = PHOTOCELL [package=photocell-kit]
  R10 = PHOTOCELL [package=photocell-kit]
  LED1 = smd LED [color="Red (660nm)" package="0603 [SMD]"]  # not connected
  R11 = Resistor [tolerance=±5% resistance=10k package=THT]
  MCP1 = MCP3208

nets:
  N1: A1.3V3, S4.Pin_3, S4.Pin_4, R2.P$2, R8.P$2, R9.P$2, R10.P$2
  N2: A1.GND, R1.Pin_0, R4.Pin_1, R5.Pin_1, R6.Pin_1, R7.Pin_1, R11.Pin_1
  N3: A1.GPIO17, IC1.In_1
  N4: A1.GPIO27, IC1.In_2
  N5: A1.GPIO22, IC1.In_3
  N6: A1.GPIO23, IC1.In_4
  N7: A1.GPIO26, S4.Pin_1, S4.Pin_2, R11.Pin_0
  N8: R2.P$1, R4.Pin_0, MCP1.Chan_0, MCP1.VDD
  N9: R5.Pin_0, R9.P$1, MCP1.Chan_2, MCP1.AGND
  N10: R6.Pin_0, R8.P$1, MCP1.Chan_1, MCP1.VREF
  N11: R7.Pin_0, R10.P$1, MCP1.Chan_3, MCP1.CLK
  N12: MCP1.Chan_4, MCP1.DOUT
  N13: MCP1.Chan_5, MCP1.DIN
  N14: MCP1.Chan_6, MCP1.CS/SHDN
  N15: MCP1.Chan_7, MCP1.DGND

custom parts:
  Raspberry Pi 5: The RPi5, a faster version of the awesome Raspberry Pi4B ARM Board with 40 pin gpio.
